// Logisim project control-logic.circ as structural Verilog: 1 circuit, main circuit control_logic
module control_logic (
  input  [31:0] Instruction,
  input  BrEq,
  input  BrLt,
  output PCSel,
  output RegWEn,
  output [2:0] ImmSel,
  output BrUn,
  output ASel,
  output BSel,
  output [3:0] ALUSel,
  output MemWEn,
  output [1:0] WBSel
);

  wire and_1_out, and_2_out, and_3_out, and_4_out, B, f30, f31, f32, f33, f34, f35, f36, f37, f700, f701,
       f720, i0, I1, i1_t, I2, i2_t, i3, i4, i5, i6, i7, i8, i9, i10, i11, i12, i13, i14, i15, i16, i17, i18,
       i19, i20, i21, i22, i23, i24, i25, i26, i27, i28, i29, i30, i31, i32, i33, i34, i35, not_1_out,
       not_2_out, or_1_out, or_2_out, R, S;
  wire [5:0] rom_in;
  wire [15:14] rom_1_data;

  ROM #(.addrWidth(6), .dataWidth(16)) rom_1 (
    .addr(rom_in), .data({rom_1_data, WBSel, MemWEn, ALUSel, BSel, ASel, BrUn, ImmSel, RegWEn}));
  Priority_Encoder #(.select_enc(6)) priority_encoder_1 (
    .in0(i0), .in1(i1_t), .in2(i2_t), .in3(i3), .in4(i4), .in5(i5), .in6(i6), .in7(i7), .in8(i8), .in9(i9),
    .in10(i10), .in11(i11), .in12(i12), .in13(i13), .in14(i14), .in15(i15), .in16(i16), .in17(i17),
    .in18(i18), .in19(i19), .in20(i20), .in21(i21), .in22(i22), .in23(i23), .in24(i24), .in25(i25),
    .in26(i26), .in27(i27), .in28(i28), .in29(i29), .in30(i30), .in31(i31), .in32(i32), .in33(i33),
    .in34(i34), .in35(i35), .out(rom_in), .en_in(1'b1));  // open: in36, in37, in38, in39, in40, in41, in42, in43, in44, in45, in46, in47, in48, in49, in50, in51, in52, in53, in54, in55, in56, in57, in58, in59, in60, in61, in62, in63, gs, en_out
  or or_1 (or_1_out, i28, i30);
  or or_2 (or_2_out, i29, i31);
  not not_1 (not_1_out, BrLt);
  not not_2 (not_2_out, BrEq);
  Comparator #(.width(7)) comparator_1 (.a(Instruction[6:0]), .b(7'b0110011), .eq(R));  // open: gt, lt
  Comparator #(.width(7)) comparator_2 (.a(Instruction[6:0]), .b(7'b0000011), .eq(I1));  // open: gt, lt
  Comparator #(.width(7)) comparator_3 (.a(Instruction[6:0]), .b(7'b0010011), .eq(I2));  // open: gt, lt
  Comparator #(.width(7)) comparator_4 (.a(Instruction[6:0]), .b(7'b0100011), .eq(S));  // open: gt, lt
  Comparator #(.width(7)) comparator_5 (.a(Instruction[6:0]), .b(7'b1100011), .eq(B));  // open: gt, lt
  Comparator #(.width(7)) comparator_6 (.a(Instruction[6:0]), .b(7'b0010111), .eq(i32));  // open: gt, lt
  Comparator #(.width(7)) comparator_7 (.a(Instruction[6:0]), .b(7'b0110111), .eq(i33));  // open: gt, lt
  Comparator #(.width(7)) comparator_8 (.a(Instruction[6:0]), .b(7'b1101111), .eq(i34));  // open: gt, lt
  Comparator #(.width(7)) comparator_9 (.a(Instruction[6:0]), .b(7'b1100111), .eq(i35));  // open: gt, lt
  and and_1 (and_1_out, or_1_out, BrLt);
  and and_2 (and_2_out, or_2_out, not_1_out);
  and and_3 (and_3_out, i26, BrEq);
  and and_4 (and_4_out, i27, not_2_out);
  Decoder #(.select(3)) decoder_1 (
    .out0(f30), .out1(f31), .out2(f32), .out3(f33), .out4(f34), .out5(f35), .out6(f36), .out7(f37),
    .sel(Instruction[14:12]), .en(1'b1));
  or or_3 (PCSel, and_1_out, and_2_out, and_3_out, and_4_out);
  Comparator #(.width(7)) comparator_10 (.a(Instruction[31:25]), .b({7{1'b0}}), .eq(f700));  // open: gt, lt
  Comparator #(.width(7)) comparator_11 (.a(Instruction[31:25]), .b(7'b0100000), .eq(f720));  // open: gt, lt
  Comparator #(.width(7)) comparator_12 (.a(Instruction[31:25]), .b(7'b0000001), .eq(f701));  // open: gt, lt
  and and_5 (i19, f700, f35, I2);
  and and_6 (i20, f720, f35, I2);
  and and_7 (i26, f30, B);
  and and_8 (i27, f31, B);
  and and_9 (i28, f34, B);
  and and_10 (i29, f35, B);
  and and_11 (i30, f36, B);
  and and_12 (i31, f37, B);
  and and_13 (i0, f700, f30, R);
  and and_14 (i1_t, f701, f30, R);
  and and_15 (i2_t, f720, f30, R);
  and and_16 (i3, f700, f31, R);
  and and_17 (i4, f701, f31, R);
  and and_18 (i8, f700, f35, R);
  and and_19 (i9, f720, f35, R);
  and and_20 (i23, f30, S);
  and and_21 (i24, f31, S);
  and and_22 (i25, f32, S);
  and and_23 (i12, f30, I1);
  and and_24 (i13, f31, I1);
  and and_25 (i14, f32, I1);
  and and_26 (i15, f30, I2);
  and and_27 (i16, f31, I2);
  and and_28 (i17, f32, I2);
  and and_29 (i18, f34, I2);
  and and_30 (i21, f36, I2);
  and and_31 (i22, f37, I2);
  and and_32 (i5, f33, R);
  and and_33 (i6, f32, R);
  and and_34 (i7, f34, R);
  and and_35 (i10, f36, R);
  and and_36 (i11, f37, R);

  // Other names for the same wires on the sheet: opcode[6:0] = Instruction[6:0]; func3[2:0] = Instruction[14:12];
  //   func7[6:0] = Instruction[31:25]

  // Notes on the sheet:
  //   INPUTS to your circuit
  //   Connect ROM Input here ->
  //   contents of rom_1 (hex, n*v repeats v):
  //   1001 1401 1601 1081 1481 1581 1101 1201 1281 1681 1301 1381 41 41 41 1041 10c1 1141 1241 12c1 16c1
  //   1341 13c1 3842 3842 3842
  //   ROM FOR CONTROL LOGIC
  //   DON'T CHANGE THE LOCATIONS OF THE INPUTS AND OUTPUTS!
  //   This is only if you choose to do the ROM option
  //   CONNECT
  //   WIRE
  //   TO
  //   USE
  //   ROM
  //   OUTPUT from your circuit
  //   Reminder: If using ROM, use combinational logic for PCSel
endmodule
